# Fritzing sketch ControlReceiverAndPropulsionSystem (saved by Fritzing 0.9.1b)
breadboards: 1

parts:
  Arduino = Arduino Uno (Rev3)
  RearWheelMotor = DC Motor  # not connected
  FrontWheelMotor = DC Motor  # not connected
  MotorBattery1 = Battery Holders [package=battery-aa]
  MotorBattery2 = Battery Holders [package=battery-aa]
  MotorBattery3 = Battery Holders [package=battery-aa]  # not connected
  U1 = BATTERY-2 [package=battery-aa]
  U2 = BATTERY-2 [package=battery-aa]
  U3 = BATTERY-2 [package=battery-aa]
  U4 = BATTERY-2 [package=battery-aa]
  ForwardLED = smd LED [color="Red (660nm)" package="0603 [SMD]"]
  LeftLED = smd LED [color="Yellow (574nm)" package="0603 [SMD]"]
  RightLED = smd LED [color="Green (570nm)" package="0603 [SMD]"]

nets:
  N1: Arduino.D8, ForwardLED.anode
  N2: Arduino.D10_PWM/SS, Arduino.GND, ForwardLED.cathode, LeftLED.cathode, LeftLED.anode, RightLED.cathode
  N3: Arduino.D11_PWM/MOSI, RightLED.anode
  N4: MotorBattery1.+, MotorBattery2.-
  N5: U1.-1, U2.+1
  N6: U2.-1, U3.+1
  N7: U3.-1, U4.+1

notes:
  3.6V Rechargable
  600mAh
  6V
  ??mAh
